# Fritzing sketch aday_soru_2 (saved by Fritzing 0.9.3b)

parts:
  Parça1 = ESP-WROOM-32 [ESP-32S] Module [part_number=ESP-WROOM-32]
  GY1 = MPU-6050 Board GY-521 [form="♀ (female)" package=THT]

nets:
  N1: Parça1.GND, GY1.pin2
  N2: Parça1.3V3, GY1.pin1
  N3: Parça1.IO21, GY1.pin4
  N4: Parça1.IO22, GY1.pin3

custom parts:
  ESP-WROOM-32 [ESP-32S] Module: Espressif ESP-WROOM-32 WiFi/Bluetooth LE microcontroller module also known as the Ai-Thinker ESP-32S module with similar formfactor. The ESP32 is a microcontroller chip with WiFi and BLE capabilities. The chip is developed by Espressif and is the successor to the popular ESP8266 WiFi module.
  MPU-6050 Board GY-521: Acelerometro y Giroscopio MPU-6050 Board GY-521
